# Fritzing sketch Fritzing Capstone (saved by Fritzing 0.9.3b)

parts:
  Part1 = Arduino Uno (Rev3)
  KY-1 = Keyes Relay [package=THT]
  KY-2 = Keyes Relay [package=THT]
  PIR1 = PIR sensor
  KY-4 = Keyes Relay [package=THT]
  KY-5 = Keyes Relay [package=THT]
  Display1 = LCD screen 16x2 IIC [part_number=101290]
  AM1 = AM2302 Humidity and Temperature Sensor
  LED1 = LEDs [package=led10mm]
  F1 = Fan - Ventilador [package=THT]
  F2 = Fan - Ventilador [package=THT]
  F3 = Fan - Ventilador [package=THT]
  KY-6 = Keyes Relay [package=THT]
  PIR2 = PIR sensor

nets:
  N1: Part1.A4/SDA, Display1.SCL
  N2: Part1.A5/SCL, Display1.SDA
  N3: Part1.D8, PIR1.SIG
  N4: Part1.D9_PWM, PIR2.SIG
  N5: Part1.D2, AM1.DATA
  N6: Part1.D3_PWM, KY-4.signal
  N7: Part1.D4, KY-2.signal
  N8: Part1.D5_PWM, KY-1.signal
  N9: Part1.D6_PWM, KY-5.signal
  N10: Part1.D7, KY-6.signal
  N11: Part1.5V, KY-6.power
  N12: KY-1.NO, F3.5V
  N13: KY-2.C, KY-6.NO
  N14: KY-2.NO, F2.5V
  N15: KY-4.NO, F1.5V
  N16: KY-5.C, LED1.A

notes:
  Input Power AC

custom parts:
  Keyes Relay: The Keyes 5V relay module is suitable for SCM development, home appliance control. It uses a 5V~12V TIL control signal which can control DC / AC signal.
  LCD screen 16x2 IIC: LCD screen with HD44780 controller enables showing text, symbols, value or anything else that comes from Croduino/Arduino. It is capable of showing 16 symbols in two lines and therefore can be used in many projects that need to send clearly visible and legible output information.. • Color of symbols: White • Backlight: Blue • Dimensions: 80 x 36 x 12 mm • Screen dimensions: 64.5 x 16 mm •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
  LEDs: LEDs Standard schematic elements and footprints for 5mm, 3mm, 1206, and 0603 sized LEDs. 5mm - Spark Fun Electronics SKU : COM-00529 (and others)
  Fan - Ventilador: Ventilador de 2 pines, se encuentra comunmente en computadoras de escritorio
